# Fritzing sketch clock_control (saved by Fritzing 0.9.3b)
breadboards: 1

parts:
  R1 = Resistor [tolerance=±5% resistance=47 package=THT]
  R2 = Resistor [tolerance=±5% resistance=47 package=THT]
  U1 = DIODE-ZENER [package=diode-zener]
  U2 = DIODE-ZENER [package=diode-zener]
  Part1 = Arduino Uno (Rev3) - ICSP
  MCU1 = Raspberry Pi Zero  # not connected

nets:
  N1: R1.Pin_0, Part1.D4
  N2: R1.Pin_1, U1.C
  N3: R2.Pin_0, Part1.D3_PWM
  N4: R2.Pin_1, U2.C
  GND: U1.A, U2.A, Part1.GND
